// Logisim project Main.circ as structural Verilog: 5 circuits, main circuit main
module main (
);

  wire clock_1_out, RESET_IP_out;
  wire [7:0] adder_1_out, IP_q, ula_1_res;
  wire [23:0] MI_data;
  wire [31:0] bancoreg_1_o1, bancoreg_1_o2;
  wire [31:8] ula_1_res_2;

  Clock clock_1 (.out(clock_1_out));
  Register IP (.D(adder_1_out), .en(1'b1), .clk(clock_1_out), .Q(IP_q), .clr(RESET_IP_out));
  Adder adder_1 (.a(8'h1), .b(IP_q), .out(adder_1_out));  // open: cin, cout
  Button RESET_IP (.out(RESET_IP_out));
  ROM #(.dataWidth(24)) MI (.addr(IP_q), .data(MI_data));
  BancoReg bancoreg_1 (
    .CLK(clock_1_out), .D({ula_1_res_2, ula_1_res}), .RS1(MI_data[12:9]), .RS2(MI_data[16:13]),
    .RD(MI_data[5:2]), .O1(bancoreg_1_o1), .O2(bancoreg_1_o2));  // open: W
  ULA ula_1 (.OP1(bancoreg_1_o1), .OP2(bancoreg_1_o2), .RES({ula_1_res_2, ula_1_res}));  // open: OPR
  RAM #(.dataWidth(32), .enables("line")) MD (.addr(ula_1_res), .clk(clock_1_out));  // open: we, din, dout
endmodule

module BancoReg (
  input  CLK,
  input  [31:0] D,
  input  [3:0] RS1,
  input  [3:0] RS2,
  input  [3:0] RD,
  input  W,
  output [31:0] O1,
  output [31:0] O2
);

  wire demultiplexer_1_out0, demultiplexer_1_out1, demultiplexer_1_out2, demultiplexer_1_out3,
       demultiplexer_1_out4, demultiplexer_1_out5, demultiplexer_1_out6, demultiplexer_1_out7,
       demultiplexer_1_out8, demultiplexer_1_out9, demultiplexer_1_out10, demultiplexer_1_out11,
       demultiplexer_1_out12, demultiplexer_1_out13, demultiplexer_1_out14, demultiplexer_1_out15;
  wire [31:0] register_1_q, register_2_q, register_3_q, register_4_q, register_5_q, register_6_q,
       register_7_q, register_8_q, register_9_q, register_10_q, register_11_q, register_12_q, register_13_q,
       register_14_q, register_15_q, register_16_q;

  Demultiplexer #(.select(4)) demultiplexer_1 (
    .out0(demultiplexer_1_out0), .out1(demultiplexer_1_out1), .out2(demultiplexer_1_out2),
    .out3(demultiplexer_1_out3), .out4(demultiplexer_1_out4), .out5(demultiplexer_1_out5),
    .out6(demultiplexer_1_out6), .out7(demultiplexer_1_out7), .out8(demultiplexer_1_out8),
    .out9(demultiplexer_1_out9), .out10(demultiplexer_1_out10), .out11(demultiplexer_1_out11),
    .out12(demultiplexer_1_out12), .out13(demultiplexer_1_out13), .out14(demultiplexer_1_out14),
    .out15(demultiplexer_1_out15), .in(W), .sel(RD));
  Register #(.width(32)) register_1 (.D(D), .en(demultiplexer_1_out0), .clk(CLK), .Q(register_1_q), .clr(1'b1));
  Register #(.width(32)) register_2 (.D(D), .en(demultiplexer_1_out1), .clk(CLK), .Q(register_2_q));  // open: clr
  Register #(.width(32)) register_3 (.D(D), .en(demultiplexer_1_out2), .clk(CLK), .Q(register_3_q));  // open: clr
  Register #(.width(32)) register_4 (.D(D), .en(demultiplexer_1_out3), .clk(CLK), .Q(register_4_q));  // open: clr
  Register #(.width(32)) register_5 (.D(D), .en(demultiplexer_1_out4), .clk(CLK), .Q(register_5_q));  // open: clr
  Register #(.width(32)) register_6 (.D(D), .en(demultiplexer_1_out5), .clk(CLK), .Q(register_6_q));  // open: clr
  Register #(.width(32)) register_7 (.D(D), .en(demultiplexer_1_out6), .clk(CLK), .Q(register_7_q));  // open: clr
  Register #(.width(32)) register_8 (.D(D), .en(demultiplexer_1_out7), .clk(CLK), .Q(register_8_q));  // open: clr
  Register #(.width(32)) register_9 (.D(D), .en(demultiplexer_1_out8), .clk(CLK), .Q(register_9_q));  // open: clr
  Register #(.width(32)) register_10 (.D(D), .en(demultiplexer_1_out9), .clk(CLK), .Q(register_10_q));  // open: clr
  Register #(.width(32)) register_11 (.D(D), .en(demultiplexer_1_out10), .clk(CLK), .Q(register_11_q));  // open: clr
  Register #(.width(32)) register_12 (.D(D), .en(demultiplexer_1_out11), .clk(CLK), .Q(register_12_q));  // open: clr
  Register #(.width(32)) register_13 (.D(D), .en(demultiplexer_1_out12), .clk(CLK), .Q(register_13_q));  // open: clr
  Register #(.width(32)) register_14 (.D(D), .en(demultiplexer_1_out13), .clk(CLK), .Q(register_14_q));  // open: clr
  Register #(.width(32)) register_15 (.D(D), .en(demultiplexer_1_out14), .clk(CLK), .Q(register_15_q));  // open: clr
  Register #(.width(32)) register_16 (.D(D), .en(demultiplexer_1_out15), .clk(CLK), .Q(register_16_q));  // open: clr
  Multiplexer #(.select(4), .width(32)) multiplexer_1 (
    .in0(register_1_q), .in1(register_2_q), .in2(register_3_q), .in3(register_4_q), .in4(register_5_q),
    .in5(register_6_q), .in6(register_7_q), .in7(register_8_q), .in8(register_9_q), .in9(register_10_q),
    .in10(register_11_q), .in11(register_12_q), .in12(register_13_q), .in13(register_14_q),
    .in14(register_15_q), .in15(register_16_q), .out(O1), .sel(RS1));
  Multiplexer #(.select(4), .width(32)) multiplexer_2 (
    .in0(register_1_q), .in1(register_2_q), .in2(register_3_q), .in3(register_4_q), .in4(register_5_q),
    .in5(register_6_q), .in6(register_7_q), .in7(register_8_q), .in8(register_9_q), .in9(register_10_q),
    .in10(register_11_q), .in11(register_12_q), .in12(register_13_q), .in13(register_14_q),
    .in14(register_15_q), .in15(register_16_q), .out(O2), .sel(RS2));
endmodule

module ULA (
  input  [3:0] OPR,
  input  [31:0] OP1,
  input  [31:0] OP2,
  output [31:0] RES
);

  wire [31:0] ADD, ANDx, DIV, MODx, MUL, ORx, SLLx, SUB, XORx;

  Adder #(.width(32)) adder_1 (.a(OP1), .b(OP2), .out(ADD));  // open: cin, cout
  Subtractor #(.width(32)) subtractor_1 (.a(OP1), .b(OP2), .out(SUB));  // open: bin, bout
  Divider #(.mode("twosComplement"), .width(32)) divider_1 (.a(OP1), .b(OP2), .out(DIV), .rem(MODx));  // open: upper
  Multiplier #(.mode("twosComplement"), .width(32)) multiplier_1 (.a(OP1), .b(OP2), .out(MUL));  // open: cin, cout
  assign ANDx = OP1 & OP2;  // AND_Gate and_1, 32 bits wide
  assign ORx = OP1 | OP2;  // OR_Gate or_1, 32 bits wide
  assign XORx = OP1 ^ OP2;  // XOR_Gate xor_1, 32 bits wide
  Shifter #(.width(32)) shifter_1 (.in(OP1), .\dist (OP2[4:0]), .out(SLLx));
  Multiplexer #(.select(4), .width(32)) multiplexer_1 (
    .in0(ADD), .in1(SUB), .in2(MUL), .in3(DIV), .in4(MODx), .in5(ANDx), .in6(ORx), .in7(XORx), .in8(ADD),
    .in9(ADD), .in10(ADD), .in11(SLLx), .in12(MODx), .in13(ANDx), .in14(ORx), .in15(XORx), .out(RES),
    .sel(OPR));
endmodule

module Branch (
  input  [1:0] OPR,
  input  [31:0] OP1,
  input  [31:0] OP2,
  output RES
);

  wire comparator_1_eq, comparator_1_gt, comparator_1_lt, not_1_out, or_1_out;

  Comparator #(.width(32)) comparator_1 (
    .a(OP1), .b(OP2), .gt(comparator_1_gt), .eq(comparator_1_eq), .lt(comparator_1_lt));
  or or_1 (or_1_out, comparator_1_eq, comparator_1_gt);
  not not_1 (not_1_out, comparator_1_eq);
  Multiplexer #(.select(2)) multiplexer_1 (
    .in0(comparator_1_eq), .in1(not_1_out), .in2(or_1_out), .in3(comparator_1_lt), .out(RES), .sel(OPR));
endmodule

module Imm (
  input  [23:0] INST,
  output [31:0] RES
);

  Multiplexer #(.select(2), .width(32)) multiplexer_1 (
    .in1({{22{INST[23]}}, INST[22:13]}), .in2({{22{INST[23]}}, INST[22:17], INST[5:2]}),
    .in3({{17{INST[23]}}, INST[22:8]}), .out(RES), .sel(INST[1:0]));  // open: in0
endmodule
